// Logisim project arithmetic_logic.circ as structural Verilog: 11 circuits, main circuit main
module main (
  input  [8:0] Sign,
  input  [8:0] Sign_2,
  output [7:0] out_3,
  output out_4,
  output out_5
);

  wire and_1_out, and_2_out, and_3_out, and_4_out, and_5_out, button_1_out, control_unit_1_negate, not_1_out,
       overflowdetection_1_v, synchroniser_1_clk;
  wire [1:0] synchroniser_1_counter;
  wire [7:0] control_unit_1_outa, control_unit_1_outb, register_8bit_1_q;

  Button button_1 (.out(button_1_out));
  Synchroniser synchroniser_1 (.\input (button_1_out), .Counter(synchroniser_1_counter), .CLK(synchroniser_1_clk));
  register_8bit register_8bit_1 (.D(out_3), .CLK(synchroniser_1_clk), .Q(register_8bit_1_q));  // open: Qcomplement
  Control_unit control_unit_1 (
    .Counter(synchroniser_1_counter), .SUB_A(Sign[8]), .SUB_B(Sign_2[8]), .F(register_8bit_1_q),
    .A(Sign[7:0]), .B(Sign_2[7:0]), .OUTA(control_unit_1_outa), .OUTB(control_unit_1_outb),
    .Negate(control_unit_1_negate));
  not not_1 (not_1_out, synchroniser_1_counter[1]);
  and and_1 (and_1_out, synchroniser_1_counter[0], not_1_out);
  and and_2 (and_2_out, and_1_out, Sign[8]);
  and and_3 (and_3_out, and_1_out, Sign_2[8]);
  adder_8bit adder_8bit_1 (
    .SUB_B(and_3_out), .SUB_A(and_2_out), .B(control_unit_1_outb), .A(control_unit_1_outa), .S(out_3));  // open: Cout
  OverflowDetection overflowdetection_1 (
    .SUB_A(Sign[8]), .SUB_B(Sign_2[8]), .NEGATE(control_unit_1_negate), .V(overflowdetection_1_v));
  and and_4 (and_4_out, synchroniser_1_counter[0], synchroniser_1_counter[1]);
  and and_5 (and_5_out, synchroniser_1_clk, and_4_out);
  D_Flip_Flop d_ff_1 (.D(control_unit_1_negate), .clk(and_5_out), .Q(out_4));  // open: Qn, preset, reset
  D_Flip_Flop d_ff_2 (.D(overflowdetection_1_v), .clk(and_5_out), .Q(out_5));  // open: Qn, preset, reset

  // Notes on the sheet:
  //   REG F
  //   A
  //   B
endmodule

module Half_adder (
  input  A,
  input  B,
  output S,
  output Cout
);

  xor xor_1 (S, A, B);
  and and_1 (Cout, B, A);
endmodule

module Full_adder (
  input  A,
  input  B,
  input  Cin,
  output S,
  output Cout
);

  wire half_adder_1_cout, half_adder_1_s, half_adder_2_cout;

  Half_adder half_adder_1 (.A(A), .B(B), .S(half_adder_1_s), .Cout(half_adder_1_cout));
  Half_adder half_adder_2 (.A(half_adder_1_s), .B(Cin), .S(S), .Cout(half_adder_2_cout));
  or or_1 (Cout, half_adder_2_cout, half_adder_1_cout);
endmodule

module adder_8bit (
  input  [7:0] A,
  input  [7:0] B,
  input  SUB_A,
  input  SUB_B,
  output Cout,
  output [7:0] S
);

  wire full_adder_1_cout, full_adder_2_cout, full_adder_3_cout, full_adder_4_cout, full_adder_5_cout,
       full_adder_6_cout, full_adder_7_cout, xor_1_out;
  wire [7:0] one_complement_8bit_1_c, one_complement_8bit_2_c;

  one_complement_8bit one_complement_8bit_1 (.A(A), .E(SUB_A), .C(one_complement_8bit_1_c));
  one_complement_8bit one_complement_8bit_2 (.A(B), .E(SUB_B), .C(one_complement_8bit_2_c));
  xor xor_1 (xor_1_out, SUB_A, SUB_B);
  Full_adder full_adder_1 (
    .A(one_complement_8bit_1_c[0]), .B(one_complement_8bit_2_c[0]), .Cin(xor_1_out), .S(S[0]),
    .Cout(full_adder_1_cout));
  Full_adder full_adder_2 (
    .A(one_complement_8bit_1_c[1]), .B(one_complement_8bit_2_c[1]), .Cin(full_adder_1_cout), .S(S[1]),
    .Cout(full_adder_2_cout));
  Full_adder full_adder_3 (
    .A(one_complement_8bit_1_c[2]), .B(one_complement_8bit_2_c[2]), .Cin(full_adder_2_cout), .S(S[2]),
    .Cout(full_adder_3_cout));
  Full_adder full_adder_4 (
    .A(one_complement_8bit_1_c[3]), .B(one_complement_8bit_2_c[3]), .Cin(full_adder_3_cout), .S(S[3]),
    .Cout(full_adder_4_cout));
  Full_adder full_adder_5 (
    .A(one_complement_8bit_1_c[4]), .B(one_complement_8bit_2_c[4]), .Cin(full_adder_4_cout), .S(S[4]),
    .Cout(full_adder_5_cout));
  Full_adder full_adder_6 (
    .A(one_complement_8bit_1_c[5]), .B(one_complement_8bit_2_c[5]), .Cin(full_adder_5_cout), .S(S[5]),
    .Cout(full_adder_6_cout));
  Full_adder full_adder_7 (
    .A(one_complement_8bit_1_c[6]), .B(one_complement_8bit_2_c[6]), .Cin(full_adder_6_cout), .S(S[6]),
    .Cout(full_adder_7_cout));
  Full_adder full_adder_8 (
    .A(one_complement_8bit_1_c[7]), .B(one_complement_8bit_2_c[7]), .Cin(full_adder_7_cout), .S(S[7]),
    .Cout(Cout));
endmodule

module two_complement_8bit (
  input  [7:0] A,
  input  E,
  output [7:0] C
);

  wire [7:0] xor_1_out;

  xor xor_1 (xor_1_out[0], A[0], E);
  xor xor_2 (xor_1_out[1], A[1], E);
  xor xor_3 (xor_1_out[2], A[2], E);
  xor xor_4 (xor_1_out[3], A[3], E);
  xor xor_5 (xor_1_out[4], A[4], E);
  xor xor_6 (xor_1_out[5], A[5], E);
  xor xor_7 (xor_1_out[6], A[6], E);
  xor xor_8 (xor_1_out[7], A[7], E);
  adder_8bit adder_8bit_1 (.SUB_B(1'b0), .SUB_A(1'b0), .B({{7{1'b0}}, E}), .A(xor_1_out), .S(C));  // open: Cout
endmodule

module one_complement_8bit (
  input  [7:0] A,
  input  E,
  output [7:0] C
);

  xor xor_1 (C[0], A[0], E);
  xor xor_2 (C[1], A[1], E);
  xor xor_3 (C[2], A[2], E);
  xor xor_4 (C[3], A[3], E);
  xor xor_5 (C[4], A[4], E);
  xor xor_6 (C[5], A[5], E);
  xor xor_7 (C[6], A[6], E);
  xor xor_8 (C[7], A[7], E);
endmodule

module register_8bit (
  input  [7:0] D,
  input  CLK,
  output [7:0] Q,
  output [7:0] Qcomplement
);

  D_Flip_Flop d_ff_1 (.D(D[0]), .clk(CLK), .Q(Q[0]), .Qn(Qcomplement[0]));  // open: preset, reset
  D_Flip_Flop d_ff_2 (.D(D[1]), .clk(CLK), .Q(Q[1]), .Qn(Qcomplement[1]));  // open: preset, reset
  D_Flip_Flop d_ff_3 (.D(D[2]), .clk(CLK), .Q(Q[2]), .Qn(Qcomplement[2]));  // open: preset, reset
  D_Flip_Flop d_ff_4 (.D(D[3]), .clk(CLK), .Q(Q[3]), .Qn(Qcomplement[3]));  // open: preset, reset
  D_Flip_Flop d_ff_5 (.D(D[4]), .clk(CLK), .Q(Q[4]), .Qn(Qcomplement[4]));  // open: preset, reset
  D_Flip_Flop d_ff_6 (.D(D[5]), .clk(CLK), .Q(Q[5]), .Qn(Qcomplement[5]));  // open: preset, reset
  D_Flip_Flop d_ff_7 (.D(D[6]), .clk(CLK), .Q(Q[6]), .Qn(Qcomplement[6]));  // open: preset, reset
  D_Flip_Flop d_ff_8 (.D(D[7]), .clk(CLK), .Q(Q[7]), .Qn(Qcomplement[7]));  // open: preset, reset
endmodule

module clock_counter (
  input  CLK,
  input  D,
  output [1:0] out_3,
  output Done
);

  wire full_adder_1_cout, full_adder_1_s, full_adder_2_s;

  D_Flip_Flop d_ff_1 (.D(full_adder_1_s), .clk(CLK), .Q(out_3[0]));  // open: Qn, preset, reset
  Full_adder full_adder_1 (.A(D), .B(out_3[0]), .Cin(1'b0), .S(full_adder_1_s), .Cout(full_adder_1_cout));
  D_Flip_Flop d_ff_2 (.D(full_adder_2_s), .clk(CLK), .Q(out_3[1]));  // open: Qn, preset, reset
  Full_adder full_adder_2 (.A(1'b0), .B(out_3[1]), .Cin(full_adder_1_cout), .S(full_adder_2_s), .Cout(Done));
endmodule

module Synchroniser (
  input  \input ,
  output [1:0] Counter,
  output CLK
);

  wire and_1_out, and_2_out, clock_counter_1_done, d_ff_1_q, not_1_out, or_1_out;

  Clock clock_1 (.out(CLK));
  and and_1 (and_1_out, d_ff_1_q, 1'b1);
  clock_counter clock_counter_1 (.CLK(CLK), .D(and_1_out), .out_3(Counter), .Done(clock_counter_1_done));
  not not_1 (not_1_out, clock_counter_1_done);
  and and_2 (and_2_out, d_ff_1_q, not_1_out);
  D_Flip_Flop d_ff_1 (.D(or_1_out), .clk(CLK), .Q(d_ff_1_q));  // open: Qn, preset, reset
  or or_1 (or_1_out, \input , and_2_out);
endmodule

module Control_unit (
  input  [7:0] A,
  input  [7:0] B,
  input  SUB_A,
  input  SUB_B,
  input  [7:0] F,
  input  [1:0] Counter,
  output [7:0] OUTA,
  output [7:0] OUTB,
  output Negate
);

  wire [1:1] and_1_out;
  wire [7:0] one_complement_8bit_1_c;

  and and_1 (and_1_out[1], SUB_A, SUB_B);
  one_complement_8bit one_complement_8bit_1 (.A(F), .E(F[7]), .C(one_complement_8bit_1_c));
  Multiplexer #(.select(2), .width(8)) multiplexer_1 (
    .in0(one_complement_8bit_1_c), .in1(A), .in2(F), .in3(one_complement_8bit_1_c), .out(OUTA), .sel(Counter));
  Multiplexer #(.select(2), .width(8)) multiplexer_2 (
    .in0({8{1'b0}}), .in1(B), .in2({{6{1'b0}}, and_1_out[1], 1'b0}), .in3({{7{1'b0}}, F[7]}), .out(OUTB),
    .sel(Counter));

  assign Negate = F[7];
endmodule

module OverflowDetection (
  input  SUB_A,
  input  SUB_B,
  input  NEGATE,
  output V
);

  wire and_1_out, and_2_out, and_3_out, and_4_out, not_1_out, not_2_out, not_3_out;

  not not_1 (not_1_out, SUB_A);
  not not_2 (not_2_out, SUB_B);
  and and_1 (and_1_out, SUB_A, SUB_B);
  and and_2 (and_2_out, not_1_out, not_2_out);
  not not_3 (not_3_out, NEGATE);
  and and_3 (and_3_out, and_1_out, not_3_out);
  and and_4 (and_4_out, NEGATE, and_2_out);
  or or_1 (V, and_3_out, and_4_out);
endmodule
